// Logisim project sketch.circ as structural Verilog: 4 circuits, main circuit main
module Wroom32 (
  input  _3v3,
  input  GND,
  input  EN,
  input  G23,
  input  SP,
  input  G22,
  input  G34,
  input  TXD,
  input  SN,
  input  RXD,
  input  G35,
  input  G21,
  input  G32,
  input  GND_2,
  input  G33,
  input  G19,
  input  G25,
  input  G18,
  input  G26,
  input  G5,
  input  G27,
  input  G17,
  input  G14,
  input  G16,
  input  G12,
  input  G4,
  input  GND_3,
  input  G0,
  input  G13,
  input  G2,
  input  SD2,
  input  G15,
  input  SD3,
  input  SD1,
  input  CMD,
  input  SD0,
  input  V5,
  input  CLK,
  input  MICRO_USB
);
endmodule

module main (
);

  wire _3V3, GND, Toggle_Writing_out, undriven, undriven_2, undriven_3, undriven_4, undriven_5, undriven_6,
       undriven_7;

  Wroom32 wroom32_1 (
    .GND(GND), .G23(undriven), .G22(undriven_2), .TXD(undriven_3), .RXD(undriven_4), .G21(undriven_5),
    .GND_2(undriven_6), .G19(undriven_7), .G16(Toggle_Writing_out), ._3v3(_3V3), .MICRO_USB(1'b1));  // open: G18, G5, G17, G4, G0, G2, G15, SD1, SD0, CLK, EN, SP, G34, SN, G35, G32, G33, G25, G26, G27, G14, G12, GND_3, G13, SD2, SD3, CMD, V5
  LED LED (.in(undriven_6));
  Button Toggle_Writing (.out(Toggle_Writing_out));
  MPU6050 mpu6050_1 (.VCC(_3V3), .GND(GND), .SCL(undriven_2), .SDA(undriven_5));  // open: XDA, XCL, ADC, INT
  Micro_SD_Shield micro_sd_shield_1 (
    .GND(GND), .D5(undriven_3), .D6(undriven_7), .D7(undriven), .D8(undriven_4), ._3V3(_3V3));  // open: TX, RX, D1, D2, D3, D4, _5V, RST, A0, D0
endmodule

module MPU6050 (
  input  VCC,
  input  GND,
  input  SCL,
  input  SDA,
  input  XDA,
  input  XCL,
  input  ADC,
  input  INT
);
endmodule

module Micro_SD_Shield (
  input  RST,
  input  TX,
  input  A0,
  input  RX,
  input  D0,
  input  D1,
  input  D5,
  input  D2,
  input  D6,
  input  D3,
  input  D7,
  input  D4,
  input  D8,
  input  GND,
  input  _3V3,
  input  _5V
);


  // Notes on the sheet:
  //   MICRO SD SHIELD
endmodule
